# Fritzing sketch Wiring Diagram (saved by Fritzing 0.9.3b)

parts:
  Part1 = Arduino Mega ADK (Rev3)
  Part2 = RFID-RC522-v2
  J1 = Basic Servo
  HC-SR04_Sensor_1 = HC-SR04 Ultrasonic Distance Sensor
  HC-SR04_Sensor_2 = HC-SR04 Ultrasonic Distance Sensor
  LED1 = RGB LED (com. cathode, rgb) [package="5 mm [THT]"]
  LED2 = LEDs [package=led10mm]  # not connected
  LED3 = LEDs [package=led10mm]
  LED4 = LEDs [package=led10mm]  # not connected
  LED5 = LEDs [package=led10mm]  # not connected

nets:
  N1: Part1.A0, HC-SR04_Sensor_1.TRIG
  N2: Part1.A1, HC-SR04_Sensor_1.ECHO
  GND: Part1.GND, Part2.GND, J1.gnd, HC-SR04_Sensor_1.GND, HC-SR04_Sensor_2.GND, LED1.common_cathode, LED3.A
  3V3: Part1.3V3, Part2.3.3V
  VCC: Part1.5V, J1.vcc, HC-SR04_Sensor_1.VCC, LED3.C
  N3: Part1.D5_PWM, Part2.RST
  N4: Part1.D23, J1.pulse
  N5: Part1.D40, LED1.red_anode
  N6: Part1.D41, LED1.green_anode
  N7: Part1.D42, LED1.blue_anode
  N8: Part1.D50/MISO, Part2.MISO
  N9: Part1.D51/MOSI, Part2.MOSI
  N10: Part1.D52/SCK, Part2.SCK
  N11: Part1.D53/SS, Part2.SDA

notes:
  * RST/Reset RST 5
  * SPI SS SDA(SS) 53
  * SPI MOSI MOSI 51
  * SPI MISO MISO 50
  * SPI SCK SCK 52

custom parts:
  RFID-RC522-v2: A simple China made RFID-RC522 Reader; do check the pin labels, as this is a MFRC522 based clone.

// code stored in the sketch: Module2-Prototype.ino
#include <Servo.h>
Servo myservo; 


// RFID
#include <SPI.h>
#include <MFRC522.h>


#define SS_PIN 53
#define RST_PIN 5


MFRC522 mfrc522(SS_PIN, RST_PIN);


// Ultrasonic Sensor
#define trigPin A0
#define echoPin A1


// RGB
#define R 12
#define G 11
#define B 10


// defines variables
long duration;
int distance;


// Define the list of UIDs
byte knownUIDs[][4] = {
  {0x83, 0x56, 0xD7, 0x0F}, // card
  {0x23, 0xF1, 0xB0, 0x0D},  // keychain
};


void setup() {
  pinMode(trigPin, OUTPUT); // Sets the trigPin as an Output
  pinMode(echoPin, INPUT); // Sets the echoPin as an Input
  Serial.begin(9600); // Starts the serial communication


  myservo.attach(13);  // attaches the servo on pin 9 to the servo object


  SPI.begin();      
  mfrc522.PCD_Init();


  pinMode(R, OUTPUT);   // Initialize the digital pin as an output
  pinMode(B, OUTPUT); // Initialize the digital pin as an output
  pinMode(G, OUTPUT);  // Initialize the digital pin as an output


  setColor(255, 0, 0);
}
void loop() {


      
  carPresence();


  if (mfrc522.PICC_IsNewCardPresent() && mfrc522.PICC_ReadCardSerial()) {
    if (isKnownUID(mfrc522.uid.uidByte)) {
      Serial.println("known");
      gateOpen();
      delay(2000);
    }else{
      Serial.println("unknown");
    }
  }


}


// check if the scanned UID matches any of the known UIDs
bool isKnownUID(byte *uid) {
  // Compare the scanned UID with each known UID
  for (byte i = 0; i < sizeof(knownUIDs) / sizeof(knownUIDs[0]); i++) {
    if (compareUID(uid, knownUIDs[i], sizeof(knownUIDs[i]))) {
      return true; // UID matches a known UID
    }
  }
  return false; // UID doesn't match any known UID
}


// to compare two UIDs byte by byte
bool compareUID(byte *uid, byte *knownUID, byte size) {
  for (byte i = 0; i < size; i++) {
    if (uid[i] != knownUID[i]) {
      return false; // UID doesn't match
    }
  }
  return true; // UID matches
}


void carPresence(){
  // Clears the trigPin
  digitalWrite(trigPin, LOW);
  delayMicroseconds(2);
  // Sets the trigPin on HIGH state for 10 micro seconds
  digitalWrite(trigPin, HIGH);
  delayMicroseconds(10);
  digitalWrite(trigPin, LOW);
  // Reads the echoPin, returns the sound wave travel time in microseconds
  duration = pulseIn(echoPin, HIGH);
  // Calculating the distance
  distance = duration * 0.034 / 2;
  // Prints the distance on the Serial Monitor
  // Serial.print("Distance: ");
  // Serial.println(distance);


  if (distance > 30){
    gateClosed();
  }
}



void gateOpen(){
    myservo.write(90);
    setColor(0, 255, 0);
}


void gateClosed(){
    myservo.write(0);
    setColor(255, 0, 0);
}


// Function to set the RGB LED color
void setColor(int redValue, int greenValue, int blueValue) {
  analogWrite(R, redValue);     // Set the brightness of the red LED
  analogWrite(G, greenValue); // Set the brightness of the green LED
  analogWrite(B, blueValue);   // Set the brightness of the blue LED
}
